# Fritzing sketch House B (saved by Fritzing 1.0.1rc)
breadboards: 1

parts:
  Part1 = Arduino Leonardo (Rev3b)
  Part2 = ACS712 Low Current Sensor Board v12
  Keypad4x1 = Keypad Membran 4x4
  LCD2 = LCD screen
  LCM1602_IIC2 = LCM1602 IIC [part_number="LCM1602 IIC" chip_label="LCM1602 IIC" package="DIP (Dual Inline) [THT]"]
  VCC1 = Battery
  Boost_Convertor1 = Boost Convertor [part_number=XL6009E1 package=THT]
  LED1 = LEDs [package=led10mm]
  LED2 = LEDs [package=led10mm]
  R1 = Resistor [tolerance=±5% power=0.25 resistance=220 package=THT]
  R2 = Resistor [tolerance=±5% power=0.25 resistance=220 package=THT]
  S1 = Reed switch [package=THT]
  Q1 = MOSFET-NCHANNEL [package=to220v]
  R3 = Resistor [tolerance=±5% resistance=1k package="0402 [SMD]"]
  R4 = Resistor [tolerance=±5% power=0.25 resistance=220 package=THT]
  Q2 = MOSFET-NCHANNEL [package=to220v]
  R5 = Resistor [tolerance=±5% resistance=1k package="0402 [SMD]"]
  R6 = Resistor [tolerance=±5% power=0.25 resistance=220 package=THT]

nets:
  N1: Part1.D2/SDA, Part1.SDA, Keypad4x1.Pin8, LCM1602_IIC2.SDA
  N2: Part1.D3_PWM/SCL, Part1.SCL, Keypad4x1.Pin7, LCM1602_IIC2.SCL
  N3: Part1.D4/A6, Keypad4x1.Pin6
  N4: Part1.D6_PWM/A7, Keypad4x1.Pin4, Keypad4x1.Pin5
  N5: Part1.D7, Keypad4x1.Pin3
  5V: Part1.5V, LCM1602_IIC2.VCC
  N6: Part1.GND, Boost_Convertor1.Negative_Output, R2.Pin_0, Q1.S, R4.Pin_1
  N7: Part1.A1, R1.Pin_0, R2.Pin_1
  N8: Part1.D8/A8, Keypad4x1.Pin2
  N9: Part1.D9_PWM/A9, Keypad4x1.Pin1
  N10: Part1.D11_PWM, R5.Pin_0
  N11: Part2.IP+, LED1.A
  N12: Part2.IP-, Boost_Convertor1.Positive_Output, R1.Pin_1
  VSS: LCD2.VSS, LCM1602_IIC2.VSS
  VDD: LCD2.VDD, LCM1602_IIC2.VDD
  N13: LCD2.V0, LCM1602_IIC2.V0
  N14: LCD2.RS, LCM1602_IIC2.RS
  N15: LCD2.R/W, LCM1602_IIC2.RW
  N16: LCD2.E, LCM1602_IIC2.E
  N17: LCD2.DB0, LCM1602_IIC2.D0
  N18: LCD2.DB1, LCM1602_IIC2.D1
  N19: LCD2.DB2, LCM1602_IIC2.D2
  N20: LCD2.DB3, LCM1602_IIC2.D3
  N21: LCD2.DB4, LCM1602_IIC2.D4
  N22: LCD2.DB5, LCM1602_IIC2.D5
  N23: LCD2.DB6, LCM1602_IIC2.D6
  N24: LCD2.DB7, LCM1602_IIC2.D7
  N25: LCD2.LED+, LCM1602_IIC2.A
  N26: LCD2.LED-, LCM1602_IIC2.K
  N27: LCM1602_IIC2.LED_A, LCM1602_IIC2.LED_B
  N28: VCC1.-, Boost_Convertor1.Negative_Input
  N29: VCC1.+, Boost_Convertor1.Positive_Input
  N30: LED1.C, Q2.D
  N31: LED2.C, S1.pin_2
  N32: S1.pin_1, Q1.D, Q2.S, R6.Pin_1
  N33: Q1.G, R3.Pin_1, R4.Pin_0
  N34: Q2.G, R5.Pin_1, R6.Pin_0

notes:
  MASTER SWITCH
  BULB SWITCH
  BOOST CONVERTER
  VOLTAGE DIVIDER HOUSE

custom parts:
  Keypad Membran 4x4: Membrane Keypad 4x4 Matrix
  LCM1602 IIC: I2C-Module to use a 1602 or 2004 LCD on with the wire.h libory Serial LCD Modul
  Boost Convertor: DC to DC boost convertor
  LEDs: LEDs Standard schematic elements and footprints for 5mm, 3mm, 1206, and 0603 sized LEDs. 5mm - Spark Fun Electronics SKU : COM-00529 (and others)
