# Fritzing sketch House A (saved by Fritzing 1.0.1rc)
breadboards: 2

parts:
  Part3 = Arduino Leonardo (Rev3b)
  Keypad4x2 = Keypad Membran 4x4
  VCC2 = Battery
  Boost_Convertor2 = Boost Convertor [part_number=XL6009E1 package=THT]
  LED3 = LEDs [package=led10mm]
  R7 = Resistor [tolerance=±5% power=0.25 resistance=220 package=THT]
  R8 = Resistor [tolerance=±5% power=0.25 resistance=220 package=THT]
  Q3 = MOSFET-NCHANNEL [package=to220v]
  R9 = Resistor [tolerance=±5% resistance=1k package="0402 [SMD]"]
  R11 = Resistor [tolerance=±5% power=0.25 resistance=220 package=THT]
  LCD3 = LCD screen
  Part4 = ACS712 Low Current Sensor Board v12
  LCM1602_IIC3 = LCM1602 IIC [part_number="LCM1602 IIC" chip_label="LCM1602 IIC" package="DIP (Dual Inline) [THT]"]
  M1 = RioRand LM2596
  Part5 = ACS712 Low Current Sensor Board v12
  BAT1 = Solar Panel [package="Renogy 50 Watts 12 Volt Monocrystalline Bendable Solar Panel"]
  Q4 = MOSFET-NCHANNEL [package=to220v]
  R12 = Resistor [tolerance=±5% power=0.25 resistance=220 package=THT]
  R13 = Resistor [tolerance=±5% power=0.25 resistance=220 package=THT]
  C1 = Electrolytic Capacitor [capacitance=1µF voltage=35V package="100 mil [THT, electrolytic]"]
  C2 = Electrolytic Capacitor [capacitance=1µF voltage=35V package="100 mil [THT, electrolytic]"]
  C3 = Electrolytic Capacitor [capacitance=1µF voltage=35V package="100 mil [THT, electrolytic]"]
  C4 = Electrolytic Capacitor [capacitance=1µF voltage=35V package="100 mil [THT, electrolytic]"]
  D1 = Rectifier Diode [part_number=1N4001 package="300 mil [THT]"]
  R14 = Resistor [tolerance=±5% power=0.25 resistance=220 package=THT]  # not connected
  R15 = Resistor [tolerance=±5% power=0.25 resistance=220 package=THT]  # not connected
  BAT2 = Solar Panel [package="Renogy 50 Watts 12 Volt Monocrystalline Bendable Solar Panel"]

nets:
  N1: Part3.D2/SDA, Part3.SDA, Keypad4x2.Pin8, LCM1602_IIC3.SDA
  N2: Part3.D3_PWM/SCL, Part3.SCL, Keypad4x2.Pin7, LCM1602_IIC3.SCL
  N3: Part3.D4/A6, Keypad4x2.Pin6
  N4: Part3.D6_PWM/A7, Keypad4x2.Pin4, Keypad4x2.Pin5
  N5: Part3.D7, Keypad4x2.Pin3
  5V: Part3.5V, LCM1602_IIC3.VCC, Part5.5V
  GND: Part3.GND, Boost_Convertor2.Negative_Output, R8.Pin_0, Q3.S, R11.Pin_1, LCM1602_IIC3.GND, M1.Pin_4, Part5.GND, BAT1.-, R13.Pin_1, C1.-, C2.-, C3.-, C4.-
  N6: Part3.A1, R7.Pin_0, R8.Pin_1
  N7: Part3.A2, Part5.VO
  N8: Part3.D8/A8, Keypad4x2.Pin2
  N9: Part3.D9_PWM/A9, Keypad4x2.Pin1
  N10: Part3.D11_PWM, R12.Pin_0
  N11: VCC2.-, Boost_Convertor2.Negative_Input
  N12: VCC2.+, Boost_Convertor2.Positive_Input
  N13: Boost_Convertor2.Positive_Output, R7.Pin_1, Part4.IP-
  N14: LED3.A, Part4.IP+
  N15: LED3.C, Q3.D
  N16: Q3.G, R9.Pin_1, R11.Pin_0
  VSS: LCD3.VSS, LCM1602_IIC3.VSS
  VDD: LCD3.VDD, LCM1602_IIC3.VDD
  N17: LCD3.V0, LCM1602_IIC3.V0
  N18: LCD3.RS, LCM1602_IIC3.RS
  N19: LCD3.R/W, LCM1602_IIC3.RW
  N20: LCD3.E, LCM1602_IIC3.E
  N21: LCD3.DB0, LCM1602_IIC3.D0
  N22: LCD3.DB1, LCM1602_IIC3.D1
  N23: LCD3.DB2, LCM1602_IIC3.D2
  N24: LCD3.DB3, LCM1602_IIC3.D3
  N25: LCD3.DB4, LCM1602_IIC3.D4
  N26: LCD3.DB5, LCM1602_IIC3.D5
  N27: LCD3.DB6, LCM1602_IIC3.D6
  N28: LCD3.DB7, LCM1602_IIC3.D7
  N29: LCD3.LED+, LCM1602_IIC3.A
  N30: LCD3.LED-, LCM1602_IIC3.K
  N31: LCM1602_IIC3.LED_A, LCM1602_IIC3.LED_B
  N32: M1.Pin_1, C3.+, C4.+, BAT2.+
  N33: M1.Pin_2, Q4.D
  N34: M1.Pin_3, D1.anode
  N35: Part5.IP-, C1.+, C2.+, D1.cathode
  N36: BAT1.+, BAT2.-
  N37: Q4.G, R12.Pin_1, R13.Pin_0

notes:
  VOLTAGE DIVIDER HOUSE
  BULB SWITCH
  Boost Converter
  SOLAR PANEL IN SERIES
  BUCK CONVERTER
  VOLTAGE DIVIDER BATTERY

custom parts:
  Keypad Membran 4x4: Membrane Keypad 4x4 Matrix
  Boost Convertor: DC to DC boost convertor
  LEDs: LEDs Standard schematic elements and footprints for 5mm, 3mm, 1206, and 0603 sized LEDs. 5mm - Spark Fun Electronics SKU : COM-00529 (and others)
  LCM1602 IIC: I2C-Module to use a 1602 or 2004 LCD on with the wire.h libory Serial LCD Modul
  Solar Panel: Renogy 50 Watts 12 Volt Solar Panel
